// Logisim project source.circ as structural Verilog: 2 circuits, main circuit main
module main (
  input  [7:0] ui_in,
  input  ena,
  input  clk,
  input  rst_n,
  input  [7:0] uio_in,
  output [7:0] uo_out,
  output [7:0] uio_oe,
  output [7:0] uio_out
);

  wire not_2_out;
  wire [7:0] not_1_out;

  Register register_1 (.D(not_1_out), .en(1'b1), .clk(clk), .Q(uo_out), .clr(not_2_out));
  assign not_1_out = ~ui_in;  // NOT_Gate not_1, 8 bits wide
  not not_2 (not_2_out, rst_n);
  Adder #(.width(2)) adder_1 (.a(uio_in[1:0]), .b(uio_in[3:2]), .out(uio_out[5:4]), .cin(1'b1), .cout(uio_out[6]));

  assign uio_oe = 8'hf0;
  assign {uio_out[7], uio_out[3:0]} = 5'b10000;

  // Notes on the sheet:
  //   uio_oe: pull=down
endmodule

module chip (
  input  [7:0] ui_in,
  input  clk,
  input  rst_n,
  input  [7:0] uio_in,
  output [7:0] uo_out,
  output [7:0] uio_out
);

  wire [7:0] and_1_out, main_1_uio_oe, main_1_uio_out, not_1_out;

  assign not_1_out = ~main_1_uio_oe;  // NOT_Gate not_1, 8 bits wide
  assign and_1_out = uio_in & not_1_out;  // AND_Gate and_1, 8 bits wide
  main main_1 (
    .ui_in(ui_in), .ena(1'b1), .clk(clk), .rst_n(rst_n), .uio_in(and_1_out), .uo_out(uo_out),
    .uio_oe(main_1_uio_oe), .uio_out(main_1_uio_out));
  assign uio_out[0] = main_1_uio_oe[0] ? main_1_uio_out[0] : 1'bz;  // Controlled_Buffer controlled_buffer_1
  assign uio_out[1] = main_1_uio_oe[1] ? main_1_uio_out[1] : 1'bz;  // Controlled_Buffer controlled_buffer_2
  assign uio_out[2] = main_1_uio_oe[2] ? main_1_uio_out[2] : 1'bz;  // Controlled_Buffer controlled_buffer_3
  assign uio_out[3] = main_1_uio_oe[3] ? main_1_uio_out[3] : 1'bz;  // Controlled_Buffer controlled_buffer_4
  assign uio_out[4] = main_1_uio_oe[4] ? main_1_uio_out[4] : 1'bz;  // Controlled_Buffer controlled_buffer_5
  assign uio_out[5] = main_1_uio_oe[5] ? main_1_uio_out[5] : 1'bz;  // Controlled_Buffer controlled_buffer_6
  assign uio_out[6] = main_1_uio_oe[6] ? main_1_uio_out[6] : 1'bz;  // Controlled_Buffer controlled_buffer_7
  assign uio_out[7] = main_1_uio_oe[7] ? main_1_uio_out[7] : 1'bz;  // Controlled_Buffer controlled_buffer_8
endmodule
